# Fritzing sketch esp32-ble4 (saved by Fritzing 0.9.3b)
breadboards: 2

parts:
  MH-ET_LIVE_ESP32_DEVKIT1 = MH-ET LIVE ESP32 DEVKIT 38 pins
  LED1 = smd LED [color="Red (633nm)" package="1206 [SMD]"]
  R1 = Resistor [tolerance=±5% resistance=220 package=THT]
  LED2 = smd LED [color="Red (633nm)" package="1206 [SMD]"]
  R2 = Resistor [tolerance=±5% resistance=220 package=THT]
  LED3 = smd LED [color="Red (633nm)" package="1206 [SMD]"]
  R3 = Resistor [tolerance=±5% resistance=220 package=THT]
  R4 = Rotary Potentiometer (Large) [maximum_resistance=100kΩ package=THT]

nets:
  N1: MH-ET_LIVE_ESP32_DEVKIT1.3V3, R4.leg2
  N2: MH-ET_LIVE_ESP32_DEVKIT1.IO32, R4.wiper
  N3: MH-ET_LIVE_ESP32_DEVKIT1.GND#58, R4.leg1
  N4: MH-ET_LIVE_ESP32_DEVKIT1.GND#64, LED1.cathode, LED2.cathode, LED3.cathode
  N5: MH-ET_LIVE_ESP32_DEVKIT1.IO19, R3.Pin_1
  N6: MH-ET_LIVE_ESP32_DEVKIT1.IO18, R2.Pin_1
  N7: MH-ET_LIVE_ESP32_DEVKIT1.IO5, R1.Pin_1
  N8: LED1.anode, R1.Pin_0
  N9: LED2.anode, R2.Pin_0
  N10: LED3.anode, R3.Pin_0

custom parts:
  MH-ET LIVE ESP32 DEVKIT 38 pins: http://mh.nodebb.com/topic/2/mh-et-live-esp32-devkit
