# Fritzing sketch schematic (saved by Fritzing 0.9.3b)
breadboards: 1

parts:
  MH-ET_LIVE_ESP32_DEVKIT1 = MH-ET LIVE ESP32 DEVKIT 38 pins
  LED1 = LED - 5mm [color="Red (633nm)" package="5 mm [THT]"]
  LED2 = LED - 5mm [color="Red (633nm)" package="5 mm [THT]"]
  LED3 = LED - 5mm [color="Red (633nm)" package="5 mm [THT]"]
  R1 = Resistor [tolerance=±5% resistance=220 package="1206 [SMD]"]
  R2 = Resistor [tolerance=±5% resistance=220 package="1206 [SMD]"]
  R3 = Resistor [tolerance=±5% resistance=220 package="1206 [SMD]"]
  R4 = Rotary Potentiometer (Large) [maximum_resistance=100kΩ package=THT]
  LCD1 = 2.8" SPI TFT Module [part_number=MSP2807]

nets:
  N1: MH-ET_LIVE_ESP32_DEVKIT1.3V3, R4.leg1
  N2: MH-ET_LIVE_ESP32_DEVKIT1.IO34, R4.wiper
  N3: MH-ET_LIVE_ESP32_DEVKIT1.5V, LCD1.pin1, LCD1.pin8
  N4: MH-ET_LIVE_ESP32_DEVKIT1.GND#64, LED1.cathode, LED2.cathode, LED3.cathode, R4.leg2, LCD1.pin2
  N5: MH-ET_LIVE_ESP32_DEVKIT1.IO23, LCD1.pin6, LCD1.pin12
  N6: MH-ET_LIVE_ESP32_DEVKIT1.IO22, LCD1.pin11
  N7: MH-ET_LIVE_ESP32_DEVKIT1.IO19, LCD1.pin9, LCD1.pin13
  N8: MH-ET_LIVE_ESP32_DEVKIT1.IO18, LCD1.pin7, LCD1.pin10
  N9: MH-ET_LIVE_ESP32_DEVKIT1.IO5, LCD1.pin3
  N10: MH-ET_LIVE_ESP32_DEVKIT1.IO17, LCD1.pin4
  N11: MH-ET_LIVE_ESP32_DEVKIT1.IO16, LCD1.pin5
  N12: MH-ET_LIVE_ESP32_DEVKIT1.IO0, R3.Pin_1
  N13: MH-ET_LIVE_ESP32_DEVKIT1.IO2, R2.Pin_1
  N14: MH-ET_LIVE_ESP32_DEVKIT1.IO15, R1.Pin_1
  N15: LED1.anode, R1.Pin_0
  N16: LED2.anode, R2.Pin_0
  N17: LED3.anode, R3.Pin_0

custom parts:
  MH-ET LIVE ESP32 DEVKIT 38 pins: http://mh.nodebb.com/topic/2/mh-et-live-esp32-devkit
  2.8" SPI TFT Module: A generic 2.8 inch LCD TFT 320x240 display with touchscreen and SD card slot. Uses the ILI9341 controller, like the Adafruit displays of this size uses.
